// Logisim project 171044035.circ as structural Verilog: 3 circuits, main circuit main
module main (
  input  a,
  input  b,
  input  c,
  input  d,
  output out_5
);

  wire circ1_1_out_5, circ1_2_out_5, circ2_1_out_5, circ2_2_out_5, not_1_out, not_2_out, not_3_out,
       not_4_out, or_1_out, or_2_out;

  not not_1 (not_1_out, a);
  not not_2 (not_2_out, b);
  not not_3 (not_3_out, c);
  not not_4 (not_4_out, d);
  circ2 circ2_1 (.a(not_1_out), .b(not_2_out), .c(a), .d(b), .out_5(circ2_1_out_5));
  circ1 circ1_1 (.a(not_1_out), .b(b), .c(not_2_out), .d(a), .out_5(circ1_1_out_5));
  circ1 circ1_2 (.a(not_3_out), .b(d), .c(c), .d(not_4_out), .out_5(circ1_2_out_5));
  circ2 circ2_2 (.a(not_3_out), .b(not_4_out), .c(c), .d(d), .out_5(circ2_2_out_5));
  or or_1 (or_1_out, circ2_1_out_5, circ1_2_out_5);
  or or_2 (or_2_out, circ1_1_out_5, circ2_2_out_5);
  and and_1 (out_5, or_1_out, or_2_out);
endmodule

module circ1 (
  input  a,
  input  b,
  input  c,
  input  d,
  output out_5
);

  wire not_1_out, not_2_out, or_1_out, or_2_out;

  not not_1 (not_1_out, a);
  not not_2 (not_2_out, d);
  or or_1 (or_1_out, not_1_out, b);
  or or_2 (or_2_out, c, not_2_out);
  and and_1 (out_5, or_1_out, or_2_out);
endmodule

module circ2 (
  input  a,
  input  b,
  input  c,
  input  d,
  output out_5
);

  wire not_1_out, not_2_out, or_1_out, or_2_out;

  not not_1 (not_1_out, a);
  not not_2 (not_2_out, b);
  or or_1 (or_1_out, not_1_out, not_2_out);
  or or_2 (or_2_out, c, d);
  and and_1 (out_5, or_1_out, or_2_out);
endmodule
