// Logisim project 171044035.circ as structural Verilog: 1 circuit, main circuit main
module main (
  input  A,
  input  B,
  input  C,
  input  D,
  input  E,
  output out_6
);

  wire and_1_out, and_2_out, and_3_out, and_4_out, and_5_out, and_6_out, not_1_out, not_2_out, not_3_out,
       not_4_out, xnor_1_out, xnor_2_out, xnor_3_out;

  not not_1 (not_1_out, A);
  not not_2 (not_2_out, E);
  not not_3 (not_3_out, B);
  and and_1 (and_1_out, not_1_out, C);
  and and_2 (and_2_out, D, E);
  and and_3 (and_3_out, D, not_2_out);
  xnor xnor_1 (xnor_1_out, A, D);
  xnor xnor_2 (xnor_2_out, and_1_out, and_2_out);
  not not_4 (not_4_out, not_3_out);
  xnor xnor_3 (xnor_3_out, and_1_out, and_3_out);
  and and_4 (and_4_out, xnor_1_out, not_3_out, C, E);
  and and_5 (and_5_out, not_3_out, xnor_2_out);
  and and_6 (and_6_out, not_4_out, xnor_3_out);
  or or_1 (out_6, and_4_out, and_5_out, and_6_out);
endmodule
