// Logisim project 171044035.circ as structural Verilog: 1 circuit, main circuit main
module main (
  input  a,
  input  b,
  input  in_3,
  output out_4
);

  wire and_2_out, and_3_out, and_4_out, and_5_out, and_6_out, and_7_out, and_8_out, clock_1_out, d_ff_1_q,
       d_ff_2_q, n0_out, n1_out, not_1_out, not_2_out, not_3_out, not_4_out, not_5_out, or_1_out, or_2_out,
       xor_1_out;

  Clock clock_1 (.out(clock_1_out));
  not not_1 (not_1_out, a);
  not not_2 (not_2_out, b);
  D_Flip_Flop d_ff_1 (.clk(clock_1_out), .D(n0_out), .Q(d_ff_1_q), .en(in_3));  // open: Qn, preset, reset
  not not_3 (not_3_out, d_ff_1_q);
  not not_4 (not_4_out, d_ff_1_q);
  D_Flip_Flop d_ff_2 (.clk(clock_1_out), .D(n1_out), .Q(d_ff_2_q), .en(in_3));  // open: Qn, preset, reset
  and and_1 (out_4, d_ff_1_q, d_ff_2_q);
  and and_2 (and_2_out, not_3_out, d_ff_2_q, a);
  not not_5 (not_5_out, d_ff_2_q);
  and and_3 (and_3_out, d_ff_1_q, not_5_out, not_1_out);
  xor xor_1 (xor_1_out, a, d_ff_2_q);
  and and_4 (and_4_out, a, d_ff_2_q);
  and and_5 (and_5_out, not_4_out, a, not_2_out);
  and and_6 (and_6_out, a, d_ff_2_q);
  or or_1 (or_1_out, xor_1_out, and_4_out);
  or or_2 (or_2_out, and_6_out, not_1_out);
  and and_7 (and_7_out, or_1_out, d_ff_1_q, b);
  and and_8 (and_8_out, or_2_out, d_ff_1_q, b);
  or n0 (n0_out, and_2_out, and_3_out, and_7_out);
  or n1 (n1_out, and_5_out, and_8_out);
endmodule
