// Logisim project 171044035.circ as structural Verilog: 1 circuit, main circuit main
module main (
  input  req,
  input  p3s,
  input  p7s,
  input  p37s,
  input  in_5
);

  wire and_1_out, and_2_out, and_3_out, and_4_out, clock_1_out, d_ff_1_q, d_ff_2_q, n0_out, n1_out,
       not_1_out, not_2_out, not_3_out, not_4_out, not_5_out;

  Clock clock_1 (.out(clock_1_out));
  not not_1 (not_1_out, p37s);
  not not_2 (not_2_out, p3s);
  not not_3 (not_3_out, p7s);
  not not_4 (not_4_out, d_ff_1_q);
  D_Flip_Flop d_ff_1 (.clk(clock_1_out), .D(n0_out), .Q(d_ff_1_q), .en(in_5));  // open: Qn, preset, reset
  not not_5 (not_5_out, d_ff_2_q);
  D_Flip_Flop d_ff_2 (.clk(clock_1_out), .D(n1_out), .Q(d_ff_2_q), .en(in_5));  // open: Qn, preset, reset
  and and_1 (and_1_out, not_1_out, not_3_out, not_2_out, not_5_out, d_ff_1_q);
  and and_2 (and_2_out, not_1_out, p7s, not_2_out, d_ff_2_q, not_4_out);
  and and_3 (and_3_out, req, p3s, not_3_out, not_1_out, not_5_out, not_4_out);
  and and_4 (and_4_out, not_1_out, not_3_out, not_2_out, not_4_out, d_ff_2_q);
  or n0 (n0_out, and_1_out, and_2_out);
  or n1 (n1_out, and_3_out, and_4_out);
endmodule
